# Fritzing sketch miCon v1 (saved by Fritzing 0.8.7b)
breadboards: 1

parts:
  R1 = Resistor [tolerance=±5% resistance=1k package=THT]
  R2 = Resistor [tolerance=±5% resistance=1k package=THT]
  R3 = Resistor [tolerance=±5% resistance=1k package=THT]
  R4 = Resistor [tolerance=±5% resistance=1k package=THT]
  R5 = Resistor [tolerance=±5% resistance=1k package=THT]
  R6 = Resistor [tolerance=±5% resistance=1k package=THT]
  R7 = Resistor [tolerance=±5% resistance=1k package=THT]
  R8 = Resistor [tolerance=±5% resistance=1k package=THT]
  R9 = Resistor [tolerance=±5% resistance=1k package=THT]
  R10 = Resistor [tolerance=±5% resistance=1k package=THT]
  R11 = Resistor [tolerance=±5% resistance=1k package=THT]
  R12 = Resistor [tolerance=±5% resistance=1k package=THT]
  Parte1 = Arduino Uno (Rev3)
  C = Round Pushbutton
  Pitch = POT [package=pot_mammoth]
  Velocidad = SLIDER [package=slider]
  B = Round Pushbutton
  A# = Round Pushbutton
  A = Round Pushbutton
  G# = Round Pushbutton
  G = Round Pushbutton
  F# = Round Pushbutton
  F = Round Pushbutton
  E = Round Pushbutton
  D# = Round Pushbutton
  D = Round Pushbutton
  C# = Round Pushbutton
  Canal = POT [package=pot_mammoth]

nets:
  N1: R1.Pin_0, R2.Pin_0, R3.Pin_0, R4.Pin_0, R5.Pin_0, R6.Pin_0, R7.Pin_0, R8.Pin_0, R9.Pin_0, R10.Pin_0, R11.Pin_0, R12.Pin_0, Parte1.5V, Pitch.S, Velocidad.A, Canal.S
  N2: R1.Pin_1, Parte1.D2, B.leg0
  N3: R2.Pin_1, Parte1.D3_PWM, A#.leg0
  N4: R3.Pin_1, Parte1.D13/SCK, C.leg0
  N5: R4.Pin_1, Parte1.D12/MISO, C#.leg0
  N6: R5.Pin_1, Parte1.D11_PWM/MOSI, D.leg0
  N7: R6.Pin_1, Parte1.D10_PWM/SS, D#.leg0
  N8: R7.Pin_1, Parte1.D9_PWM, E.leg0
  N9: R8.Pin_1, Parte1.D8, F.leg0
  N10: R9.Pin_1, Parte1.D7, F#.leg0
  N11: R11.Pin_1, Parte1.D5_PWM, G#.leg0
  N12: R12.Pin_1, Parte1.D4, A.leg0
  N13: Parte1.A0, Velocidad.S
  N14: Parte1.A1, Pitch.A
  N15: Parte1.A2, Canal.A
  N16: Parte1.D6_PWM, G.leg0
  N17: Parte1.GND, C.leg1, Pitch.E, Velocidad.E, B.leg1, A#.leg1, A.leg1, G#.leg1, G.leg1, F#.leg1, F.leg1, E.leg1, D#.leg1, D.leg1, C#.leg1, Canal.E
